// Logisim project Barrel_Shifter_16bits_Patrick.circ as structural Verilog: 1 circuit, main circuit main
module main (
  input  [15:0] in_1,
  input  [1:0] S1_S0,
  output [15:0] out_3
);

  Multiplexer #(.select(2), .enable("false")) multiplexer_1 (
    .in0(in_1[15]), .in1(in_1[0]), .in2(in_1[14]), .out(out_3[15]), .sel(S1_S0));  // open: in3
  Multiplexer #(.select(2), .enable("false")) multiplexer_2 (
    .in0(in_1[14]), .in1(in_1[15]), .in2(in_1[13]), .out(out_3[14]), .sel(S1_S0));  // open: in3
  Multiplexer #(.select(2), .enable("false")) multiplexer_3 (
    .in0(in_1[13]), .in1(in_1[14]), .in2(in_1[12]), .out(out_3[13]), .sel(S1_S0));  // open: in3
  Multiplexer #(.select(2), .enable("false")) multiplexer_4 (
    .in0(in_1[12]), .in1(in_1[13]), .in2(in_1[11]), .out(out_3[12]), .sel(S1_S0));  // open: in3
  Multiplexer #(.select(2), .enable("false")) multiplexer_5 (
    .in0(in_1[11]), .in1(in_1[12]), .in2(in_1[10]), .out(out_3[11]), .sel(S1_S0));  // open: in3
  Multiplexer #(.select(2), .enable("false")) multiplexer_6 (
    .in0(in_1[10]), .in1(in_1[11]), .in2(in_1[9]), .out(out_3[10]), .sel(S1_S0));  // open: in3
  Multiplexer #(.select(2), .enable("false")) multiplexer_7 (
    .in0(in_1[9]), .in1(in_1[10]), .in2(in_1[8]), .out(out_3[9]), .sel(S1_S0));  // open: in3
  Multiplexer #(.select(2), .enable("false")) multiplexer_8 (
    .in0(in_1[8]), .in1(in_1[9]), .in2(in_1[7]), .out(out_3[8]), .sel(S1_S0));  // open: in3
  Multiplexer #(.select(2), .enable("false")) multiplexer_9 (
    .in0(in_1[7]), .in1(in_1[8]), .in2(in_1[6]), .out(out_3[7]), .sel(S1_S0));  // open: in3
  Multiplexer #(.select(2), .enable("false")) multiplexer_10 (
    .in0(in_1[5]), .in1(in_1[6]), .in2(in_1[4]), .out(out_3[5]), .sel(S1_S0));  // open: in3
  Multiplexer #(.select(2), .enable("false")) multiplexer_11 (
    .in0(in_1[6]), .in1(in_1[7]), .in2(in_1[5]), .out(out_3[6]), .sel(S1_S0));  // open: in3
  Multiplexer #(.select(2), .enable("false")) multiplexer_12 (
    .in0(in_1[4]), .in1(in_1[5]), .in2(in_1[3]), .out(out_3[4]), .sel(S1_S0));  // open: in3
  Multiplexer #(.select(2), .enable("false")) multiplexer_13 (
    .in0(in_1[3]), .in1(in_1[4]), .in2(in_1[2]), .out(out_3[3]), .sel(S1_S0));  // open: in3
  Multiplexer #(.select(2), .enable("false")) multiplexer_14 (
    .in0(in_1[1]), .in1(in_1[2]), .in2(in_1[0]), .out(out_3[1]), .sel(S1_S0));  // open: in3
  Multiplexer #(.select(2), .enable("false")) multiplexer_15 (
    .in0(in_1[2]), .in1(in_1[3]), .in2(in_1[1]), .out(out_3[2]), .sel(S1_S0));  // open: in3
  Multiplexer #(.select(2), .enable("false")) multiplexer_16 (
    .in0(in_1[0]), .in1(in_1[1]), .in2(in_1[15]), .out(out_3[0]), .sel(S1_S0));  // open: in3
endmodule
