// Logisim project CPU_PATRICK.circ as structural Verilog: 1 circuit, main circuit main
module main (
  input  in_1,
  output [15:0] DataPathOut
);

  wire BC, C, CLK, JB, MB, MD, MW, N, OUT, PL, PS, RW, V, Z;
  wire [1:0] rom_1_data_2;
  wire [2:0] AA, BA, DA, IR;
  wire [3:0] FS;
  wire [15:0] bit_extender_1_out, BUSA, DATAIN, DATAOUT, \main_1_saída_instructionadress ;
  wire [15:3] rom_1_data;

  PC_main main_1 (
    ._8(rom_1_data[8]), .IR_7_6(rom_1_data_2), .IR_0_2(IR),
    .\Saída_InstructionAdress (\main_1_saída_instructionadress ), .Load(OUT), .BUSA(BUSA), .PS(PS),
    .Clk(CLK), .Reset(in_1));
  BranchControl_main main_2 (.PL(PL), .JB(JB), .BC(BC), .N(N), .Z(Z), .OUT(OUT), .PS(PS));
  ControlWord_main main_3 (
    .Instruction({rom_1_data[15:8], rom_1_data_2, rom_1_data[5:3], IR}), .DA(DA), .AA(AA), .BA(BA), .MB(MB),
    .FS(FS), .MD(MD), .RW(RW), .MW(MW), .PL(PL), .JB(JB), .BC(BC));
  ROM #(.addrWidth(16), .dataWidth(16)) rom_1 (
    .addr(\main_1_saída_instructionadress ), .data({rom_1_data[15:8], rom_1_data_2, rom_1_data[5:3], IR}));  // open: sel
  Clock clock_1 (.out(CLK));
  assign bit_extender_1_out = {{13{1'b0}}, IR};  // Bit_Extender bit_extender_1
  Data_Path_16bits_Patrick_main main_4 (
    .Constante_In(bit_extender_1_out), .MB(MB), .Data_In(DATAIN), .FS(FS), .Bus_A(BUSA), .OUT(DataPathOut),
    .Bus_B(DATAOUT), .V(V), .N(N), .C(C), .Z(Z), .LE(RW), .AS(AA), .BS(BA), .DS(DA), .MD(MD), .CLK(CLK));
  RAM #(.addrWidth(16), .dataWidth(16), .bus("separate")) ram_1 (
    .addr(BUSA), .din(DATAOUT), .data(DATAIN), .str(MW), .clk(CLK), .ld(1'b1));  // open: sel, clr

  // Notes on the sheet:
  //   contents of rom_1 (hex, n*v repeats v):
  //   9803 9842 9881 98c2 9903 9942 9981 99c2 204 200 408 e000 e020
  //   Patrick Silva Menezes
endmodule
