// Logisim project Data_Path_16bits_Patrick.circ as structural Verilog: 1 circuit, main circuit main
module main (
  input  LE,
  input  [2:0] AS,
  input  [2:0] BS,
  input  [15:0] Constante_In,
  input  MB,
  input  [15:0] Data_In,
  input  [3:0] FS,
  input  MD,
  input  [2:0] DS,
  input  CLK,
  output [15:0] Bus_A,
  output [15:0] OUT,
  output [15:0] Bus_B,
  output V,
  output N,
  output C,
  output Z
);

  wire and_1_out, and_2_out, and_3_out, and_4_out, and_5_out, and_6_out, and_7_out, and_8_out,
       decoder_1_out0, decoder_1_out1, decoder_1_out2, decoder_1_out3, decoder_1_out4, decoder_1_out5,
       decoder_1_out6, decoder_1_out7;
  wire [15:0] main_1_out, multiplexer_1_out, register_1_q, register_2_q, register_3_q, register_4_q,
       register_5_q, register_6_q, register_7_q, register_8_q;

  Decoder #(.select(3)) decoder_1 (
    .out0(decoder_1_out0), .out1(decoder_1_out1), .out2(decoder_1_out2), .out3(decoder_1_out3),
    .out4(decoder_1_out4), .out5(decoder_1_out5), .out6(decoder_1_out6), .out7(decoder_1_out7), .sel(DS));  // open: en
  and and_1 (and_1_out, decoder_1_out0, LE);
  and and_2 (and_2_out, decoder_1_out1, LE);
  and and_3 (and_3_out, decoder_1_out2, LE);
  and and_4 (and_4_out, decoder_1_out3, LE);
  and and_5 (and_5_out, decoder_1_out4, LE);
  and and_6 (and_6_out, decoder_1_out5, LE);
  and and_7 (and_7_out, decoder_1_out6, LE);
  and and_8 (and_8_out, decoder_1_out7, LE);
  Register #(.width(16)) register_1 (.D(OUT), .en(and_1_out), .Q(register_1_q), .clk(CLK), .clr(1'b0));
  Register #(.width(16)) register_2 (.D(OUT), .en(and_2_out), .Q(register_2_q), .clk(CLK), .clr(1'b0));
  Register #(.width(16)) register_3 (.D(OUT), .en(and_3_out), .Q(register_3_q), .clk(CLK), .clr(1'b0));
  Register #(.width(16)) register_4 (.D(OUT), .en(and_4_out), .Q(register_4_q), .clk(CLK), .clr(1'b0));
  Register #(.width(16)) register_5 (.D(OUT), .en(and_5_out), .Q(register_5_q), .clk(CLK), .clr(1'b0));
  Register #(.width(16)) register_6 (.D(OUT), .en(and_6_out), .Q(register_6_q), .clk(CLK), .clr(1'b0));
  Register #(.width(16)) register_7 (.D(OUT), .en(and_7_out), .Q(register_7_q), .clk(CLK), .clr(1'b0));
  Register #(.width(16)) register_8 (.D(OUT), .en(and_8_out), .Q(register_8_q), .clk(CLK), .clr(1'b0));
  Multiplexer #(.select(3), .width(16)) multiplexer_1 (
    .in0(register_1_q), .in1(register_2_q), .in2(register_3_q), .in3(register_4_q), .in4(register_5_q),
    .in5(register_6_q), .in6(register_7_q), .in7(register_8_q), .out(multiplexer_1_out), .sel(BS));  // open: en
  Multiplexer #(.select(3), .width(16)) multiplexer_2 (
    .in0(register_1_q), .in1(register_2_q), .in2(register_3_q), .in3(register_4_q), .in4(register_5_q),
    .in5(register_6_q), .in6(register_7_q), .in7(register_8_q), .out(Bus_A), .sel(AS));  // open: en
  Multiplexer #(.width(16)) multiplexer_3 (
    .in0(multiplexer_1_out), .in1(Constante_In), .out(Bus_B), .sel(MB));  // open: en
  FunctionUnit_main main_1 (
    .A(Bus_A), .B(Bus_B), .S2_S1_S0_Cin(FS), .OVF(V), .NEG(N), .COUT(C), .Z(Z), .OUT(main_1_out));
  Multiplexer #(.width(16)) multiplexer_4 (.in0(main_1_out), .in1(Data_In), .out(OUT), .sel(MD));  // open: en

  // Notes on the sheet:
  //   DATA IN
  //   PATRICK SILVA MENEZES
  //   S2/S1/S0/CIN
endmodule
