// Logisim project FunctionUnit.circ as structural Verilog: 1 circuit, main circuit main
module main (
  input  [15:0] A,
  input  [15:0] B,
  input  [3:0] S2_S1_S0_Cin,
  output OVF,
  output NEG,
  output COUT,
  output Z,
  output [15:0] OUT
);

  wire and_1_out;
  wire [15:0] main_1_g, Shifter_out_3;

  and and_1 (and_1_out, S2_S1_S0_Cin[2], S2_S1_S0_Cin[3]);
  ULA_COMPLETA_main main_1 (.S2_S1_S0_Cin(S2_S1_S0_Cin), .A(A), .B(B), .OVF(OVF), .NEG(NEG), .COUT(COUT), .G(main_1_g));
  Barrel_Shifter_16bits_Patrick_main Shifter (.in_1(B), .S1_S0(S2_S1_S0_Cin[1:0]), .out_3(Shifter_out_3));
  ZERO_FILL_main main_2 (.IN(main_1_g), .out_2(Z));
  Multiplexer #(.width(16)) multiplexer_1 (
    .in0(main_1_g), .in1(Shifter_out_3), .out(OUT), .sel(and_1_out));  // open: en
endmodule
