// Logisim project ULA_COMPLETA.circ as structural Verilog: 1 circuit, main circuit main
module main (
  input  [3:0] S2_S1_S0_Cin,
  input  [15:0] A,
  input  [15:0] B,
  output OVF,
  output NEG,
  output COUT,
  output [15:0] G
);

  wire [15:0] main_1_p5, main_2_out_4;

  // ULA_Aritmética_16bits_Patrick_main main_1: pin names not known; wires that end beside it: S2_S1_S0_Cin[2:1], S2_S1_S0_Cin[0], A, B, main_1_p5, OVF, NEG, COUT
  \ULA_Lógica_16bits_Patrick_main  main_2 (.in_1(A), .in_2(B), .out_4(main_2_out_4), .S1_S0(S2_S1_S0_Cin[1:0]));
  Multiplexer #(.width(16)) multiplexer_1 (
    .in0(main_1_p5), .in1(main_2_out_4), .out(G), .sel(S2_S1_S0_Cin[3]));  // open: en

  // Notes on the sheet:
  //   PATRICK SILVA MENEZES
endmodule
