// Logisim project ZERO_FILL.circ as structural Verilog: 1 circuit, main circuit main
// OUT
module main (
  input  [15:0] IN,
  output out_2
);

  nor nor_1 (out_2, IN[0], IN[1], IN[2], IN[3], IN[4], IN[5], IN[6], IN[7], IN[9], IN[10], IN[11], IN[12], IN[13], IN[14], IN[15], IN[8]);
endmodule
